// Logisim project lab0-circuit.circ as structural Verilog: 1 circuit, main circuit lab0
module lab0 (
  input  A,
  input  B,
  input  C,
  output F
);

  wire and_1_out;

  and and_1 (and_1_out, A, B);
  or or_1 (F, and_1_out, C);

  // Notes on the sheet:
  //   C: pull=down
  //   B: pull=down
  //   Lab 0: Hello World
  //   Inputs
  //   Create the circuit shown in the lecture that represents the fuction F=A*B+C
  //   ECE2300L_LAB_0_LOGISIM_EW
  //   ELIZABETH WOO - ECE2300L.02
  //   Professor McNinch - 8/24/2021
  //   Output
endmodule
