// Logisim project lab1_circuit.circ as structural Verilog: 1 circuit, main circuit lab1
module lab1 (
  input  A,
  input  B,
  output F
);

  wire nand_1_out, nand_2_out, nand_3_out;

  nand nand_1 (nand_1_out, A, B);
  nand nand_2 (nand_2_out, A, nand_1_out);
  nand nand_3 (nand_3_out, nand_1_out, B);
  nand nand_4 (F, nand_2_out, nand_3_out);

  // Notes on the sheet:
  //   B: pull=down
  //   Lab 1: NAND/NOR Implementation
  //   Create the circuit shown in the lecture to implement an XOR gate using NAND gates
  //   ECE2300L_LAB_1_LOGISIM_EW
  //   ELIZABETH WOO - ECE2300L_02
  //   Professor McNinch - 9/2/2021
endmodule
